// Logisim project 1241_display.circ as structural Verilog: 2 circuits, main circuit display
module display (
  input  [7:0] ID,
  input  [13:0] IA
);

  wire BIT0, BIT1, BUF_L, CLK_2_4_MHz, CLK_2_4_MHz_L, DROM_L, GTMODE, GTMODE_L, HD, HDRIVE_L, HSEL_L,
       INDEX_L, LATCH_200_L, LCP, LOADC_L, LOE_L, nor_1_out, not_1_out, not_2_out, OE_L, Q_1, RD_L, TMODE_L,
       U105D_out, U170A_out, U170B_out, U170D_out, U185_q1, U185_q2, U185_q3, U185_q4, U190_c4, U195_q1,
       U195_q2, U195_q3, U195_q4, U198_qc, U198_qd, U198_rco, U265A_out, U270C_out, U275B_out, U275D_out,
       U285_q1, U285_q2, U285_q3, U285_q4, U290_c4, U295_q1, U295_q4, U298_rco, U480A_q, U480C_q, VRES_L,
       VSEL_L;
  wire [2:0] L;
  wire [7:0] R, Y;
  wire [10:0] U298_qa;
  wire [11:0] U260_y4;

  not not_1 (not_1_out, Q_1);
  ttl_74670 U295 (
    .Q1(U295_q1), .Q2(BIT1), .Q3(BIT0), .Q4(U295_q4), .RA(GTMODE), .RB(CLK_2_4_MHz), .GR(1'b0), .D2(ID[1]),
    .D3(ID[2]), .D4(ID[3]), .WA(IA[0]), .WB(IA[1]), .GW(HSEL_L), .D1(ID[0]));
  or U105D (U105D_out, TMODE_L, CLK_2_4_MHz_L);
  ttl_74157 U260 (
    .Y1(U260_y4[3]), .Y2(U260_y4[2]), .Y3(U260_y4[1]), .Y4(U260_y4[0]), .STROBE(1'b0), .SEL(U170D_out),
    .B1(IA[3]), .A2(U298_qa[2]), .B2(IA[2]), .A3(U298_qa[1]), .B3(IA[1]), .A4(U298_qa[0]), .B4(IA[0]),
    .A1(U298_qa[3]));
  and U170A (U170A_out, U298_qa[10], U105D_out);
  ttl_74393 U280 (
    .QA0(R[0]), .QA1(R[1]), .QA2(R[2]), .QA3(R[3]), .QB0(R[4]), .QB1(R[5]), .QB2(R[6]), .QB3(R[7]),
    .CLR_A(1'b0), .CLK_A(HDRIVE_L), .CLR_B(1'b0), .CLK_B(R[3]));
  ttl_74163 U298 (
    .QA(U298_qa[0]), .QB(U298_qa[1]), .QC(U298_qa[2]), .QD(U298_qa[3]), .RCO(U298_rco), .ENP(1'b1),
    .ENT(1'b1), .CLR(not_1_out), .LD(nor_1_out), .CLK(CLK_2_4_MHz), .A(U295_q1), .B(BIT1), .C(BIT0),
    .D(U295_q4));
  and U170B (U170B_out, GTMODE, CLK_2_4_MHz);
  and U170D (U170D_out, CLK_2_4_MHz_L, GTMODE_L);
  ttl_74157 U165 (
    .Y1(U260_y4[10]), .Y2(U260_y4[5]), .Y3(U260_y4[4]), .Y4(U260_y4[11]), .STROBE(1'b0), .SEL(U170D_out),
    .B1(IA[10]), .A2(U298_qa[5]), .B2(IA[5]), .A3(U298_qa[4]), .B3(IA[4]), .A4(INDEX_L), .B4(IA[11]),
    .A1(U170A_out));
  ttl_74670 U195 (
    .Q1(U195_q1), .Q2(U195_q2), .Q3(U195_q3), .Q4(U195_q4), .RA(GTMODE), .RB(CLK_2_4_MHz), .GR(1'b0),
    .D2(ID[5]), .D3(ID[6]), .D4(ID[7]), .WA(IA[0]), .WB(IA[1]), .GW(HSEL_L), .D1(ID[4]));
  nand U270C (U270C_out, R[3], R[6], R[7]);
  nand U275D (U275D_out, R[4], R[6]);
  ttl_74157 U160 (
    .Y1(U260_y4[9]), .Y2(U260_y4[8]), .Y3(U260_y4[7]), .Y4(U260_y4[6]), .STROBE(U170B_out), .SEL(U170D_out),
    .B1(IA[9]), .A2(U298_qa[8]), .B2(IA[8]), .A3(U298_qa[7]), .B3(IA[7]), .A4(U298_qa[6]), .B4(IA[6]),
    .A1(U298_qa[9]));
  xor U265A (U265A_out, 1'b1, U260_y4[11]);
  ttl_74279_sr U480B (.Q(LATCH_200_L), .S(VRES_L), .R(U270C_out));
  not not_2 (not_2_out, U198_rco);
  ttl_74163 U198 (
    .QA(U298_qa[4]), .QB(U298_qa[5]), .QC(U198_qc), .QD(U198_qd), .RCO(U198_rco), .ENP(1'b1), .ENT(U298_rco),
    .CLR(not_1_out), .LD(nor_1_out), .CLK(CLK_2_4_MHz), .A(U195_q1), .B(U195_q2), .C(U195_q3), .D(U195_q4));
  // NoConnect on U198_qc
  // NoConnect on U198_qd
  nor nor_1 (nor_1_out, ~LOADC_L, ~not_2_out);  // NOR_Gate
  mem_6116P_2 U245 (
    .OD0(Y[0]), .OD1(Y[1]), .OD2(Y[2]), .OD3(Y[3]), .OD4(Y[4]), .OD5(Y[5]), .OD6(Y[6]), .OD7(Y[7]),
    .A2(U260_y4[2]), .A3(U260_y4[3]), .A4(U260_y4[4]), .A5(U260_y4[5]), .A6(U260_y4[6]), .A7(U260_y4[7]),
    .A8(U260_y4[8]), .A9(U260_y4[9]), .A10(U260_y4[10]), .A0(U260_y4[0]), .A1(U260_y4[1]), .OE(OE_L),
    .CS(U265A_out), .WE(BUF_L), .ID0(Y[0]), .ID1(Y[1]), .ID2(Y[2]), .ID3(Y[3]), .ID4(Y[4]), .ID5(Y[5]),
    .ID6(Y[6]), .ID7(Y[7]));
  ttl_74279_ssr U480C (.Q(U480C_q), .S2(VRES_L), .R(U275D_out), .S1(LATCH_200_L));
  ttl_74670 U285 (
    .Q1(U285_q1), .Q2(U285_q2), .Q3(U285_q3), .Q4(U285_q4), .RA(U480A_q), .RB(U480C_q), .GR(1'b0),
    .D2(ID[1]), .D3(ID[2]), .D4(ID[3]), .WA(IA[0]), .WB(IA[1]), .GW(VSEL_L), .D1(ID[0]));
  mem_6116P_2 U145 (
    .OD0(Y[0]), .OD1(Y[1]), .OD2(Y[2]), .OD3(Y[3]), .OD4(Y[4]), .OD5(Y[5]), .OD6(Y[6]), .OD7(Y[7]),
    .A2(U260_y4[2]), .A3(U260_y4[3]), .A4(U260_y4[4]), .A5(U260_y4[5]), .A6(U260_y4[6]), .A7(U260_y4[7]),
    .A8(U260_y4[8]), .A9(U260_y4[9]), .A10(U260_y4[10]), .A0(U260_y4[0]), .A1(U260_y4[1]), .OE(OE_L),
    .CS(U260_y4[11]), .WE(BUF_L), .ID0(Y[0]), .ID1(Y[1]), .ID2(Y[2]), .ID3(Y[3]), .ID4(Y[4]), .ID5(Y[5]),
    .ID6(Y[6]), .ID7(Y[7]));
  ttl_74279_ssr U480A (.Q(U480A_q), .S2(U275B_out), .R(VRES_L), .S1(LATCH_200_L));
  ttl_74283 U290 (
    .E1(L[0]), .E2(L[1]), .E3(L[2]), .E4(U298_qa[6]), .C4(U290_c4), .A1(U285_q1), .A2(U285_q3), .A3(R[0]),
    .A4(R[2]), .B1(U285_q2), .B2(U285_q4), .B3(R[1]), .B4(R[3]), .C0(1'b0));
  nand U275B (U275B_out, HD, U190_c4);
  ttl_74244_joined U255 (
    .Y1(Y[0]), .Y2(Y[1]), .Y3(Y[2]), .Y4(Y[3]), .Y5(Y[4]), .Y6(Y[5]), .Y7(Y[6]), .Y8(Y[7]), .A1(ID[0]),
    .A2(ID[1]), .A3(ID[2]), .A4(ID[3]), .A5(ID[4]), .A6(ID[5]), .A7(ID[6]), .A8(ID[7]), .G(BUF_L));
  ttl_74670 U185 (
    .Q1(U185_q1), .Q2(U185_q2), .Q3(U185_q3), .Q4(U185_q4), .RA(U480A_q), .RB(U480C_q), .GR(1'b0),
    .D2(ID[5]), .D3(ID[6]), .D4(ID[7]), .WA(IA[0]), .WB(IA[1]), .GW(VSEL_L), .D1(ID[4]));
  rom_drom U175 (
    .D0(ID[0]), .D1(ID[1]), .D2(ID[2]), .D3(ID[3]), .D4(ID[4]), .D5(ID[5]), .D6(ID[6]), .D7(ID[7]),
    .OE(RD_L), .CE(DROM_L), .A1(IA[0]), .A2(IA[1]), .A3(IA[2]), .A4(IA[3]), .A5(IA[4]), .A6(IA[5]),
    .A7(IA[6]), .A8(IA[7]), .A9(IA[8]), .A10(IA[9]), .A11(IA[10]), .A12(IA[11]), .A13(IA[12]), .A14(1'b0),
    .A15(1'b1), .A16(1'b1));
  ttl_74374 U155 (
    .Q1(ID[0]), .Q2(ID[1]), .Q3(ID[2]), .Q4(ID[3]), .Q5(ID[4]), .Q6(ID[5]), .Q7(ID[6]), .Q8(ID[7]),
    .CLK(LCP), .OC(LOE_L), .D1(Y[0]), .D2(Y[1]), .D3(Y[2]), .D4(Y[3]), .D5(Y[4]), .D6(Y[5]), .D7(Y[6]),
    .D8(Y[7]));
  ttl_74283 U190 (
    .E1(U298_qa[7]), .E2(U298_qa[8]), .E3(U298_qa[9]), .E4(U298_qa[10]), .C4(U190_c4), .A1(U185_q1),
    .A2(U185_q3), .A3(R[4]), .A4(R[6]), .B1(U185_q2), .B2(U185_q4), .B3(R[5]), .B4(R[7]), .C0(U290_c4));
endmodule

module rom_drom (
  input  OE,
  input  CE,
  input  A1,
  input  A2,
  input  A3,
  input  A4,
  input  A5,
  input  A6,
  input  A7,
  input  A8,
  input  A9,
  input  A10,
  input  A11,
  input  A12,
  input  A13,
  input  A14,
  input  A15,
  input  A16,
  output D0,
  output D1,
  output D2,
  output D3,
  output D4,
  output D5,
  output D6,
  output D7
);

  wire and_1_out;
  wire [7:0] rom_1_data;

  and and_1 (and_1_out, ~OE, ~CE);  // AND_Gate
  ROM #(.addrWidth(16)) rom_1 (
    .addr({A16, A15, A14, A13, A12, A11, A10, A9, A8, A7, A6, A5, A4, A3, A2, A1}), .data(rom_1_data));
  assign {D7, D6, D5, D4, D3, D2, D1, D0} = and_1_out ? rom_1_data : 8'bz;  // Controlled_Buffer controlled_buffer_1

  // Notes on the sheet:
  //   contents of rom_1 (hex, n*v repeats v):
  //   0 d 12 a 10 17 18 1c 1d 12 c 1c 24 12 17 24 19 1b 18 10 1b e 1c 1c 3e 0 32 0 ac 3e 1 32 80 a9 1 ff f
  //   21 0 d0 11 1 d0 3e 24 77 ed b0 21 0 c0 6 4 3e 0 77 23 10 fc 11 0 8 19 6 4 77 2b 10 fc 1 17 0 21 1 e0
  //   11 56 d3 ed b0 3e 2 32 80 a9 31 15 e1 11 b e1 c3 61 e0 cd 35 27 dd 21 0 0 dd 19 dd 4e 4 d9 dd 6e 6
  //   dd 66 7 dd 5e 6 dd 56 7 dd 46 9 dd 4e 8 3e aa 13 77 ed b0 13 7a dd 6e 6 dd 66 7 dd 5e 8 dd 56 9 8 3e
  //   aa 4e b9 c2 e7 e0 3e cc 77 23 8 47 8 78 bc c2 92 e0 dd 6e 6 dd 66 7 3e cc 4e b9 c2 e7 e0 3e f0 77 23
  //   8 47 8 78 bc c2 ab e0 dd 6e 6 dd 66 7 3e f0 4e b9 c2 e7 e0 3e f 77 23 8 47 8 78 bc c2 c4 e0 13 3e f
  //   2b 4e b9 47 c2 e7 e0 1b 7a b3 c2 d8 e0 8 d9 79 e6 3 fe 0 ca d e1 8 d9 78 6 1 dd 21 0 bc dd 70 1c dd
  //   77 1d dd 74 20 dd 75 1f dd 71 1e d9 cd 3c 27 8 c9 0 0 0 b0 ff f 17 e1 c2 34 e1 31 ff bf c3 a 2 ff f
  //   a 12 15 1e 1b e 5*24 12 18 19 24 1b a 16 1 c 0 21 21 e1 11 62 d3 ed b0 1 7 0 21 2d e1 11 50 d4 ed b0
  //   d9 8 7c 4*7 e6 f 32 62 d4 7c e6 f 32 63 d4 7d 4*7 e6 f 32 64 d4 7d e6 f 32 65 d4 8 4f 4*7 e6 f 32 67
  //   d4 79 e6 f 32 68 d4 7e 4*7 e6 f 32 6a d4 7e e6 f 32 6b d4 8 7c fe b8 da 97 e1 c3 9c e1 6 2 c3 9f e1
  //   6 3 af 11 ff 3f a8 32 80 a9 8 77 1b 4e 8 ba c2 a6 e1 c3 9f e1 cd 35 27 dd 21 0 0 dd 19 d9 11 1b bc
  //   21 1b bc 7a de c 57 ed a0 ed a0 ed a0 ed a0 ed a0 ed a0 dd 6e 4 dd 66 5 dd 4e 6 dd 46 7 dd 5e 8 dd
  //   56 9 ed b0 d9 dd 7e 5 fe bc c2 fb e1 7a de c 57 eb 23 77 2b eb c3 4 e2 7a c6 c 57 eb 23 77 2b eb c3
  //   3c 27 cd 41 27 21 4 0 19 7e fe 1 3e 4 20 1 f 32 a1 be cd bf b 21 1 0 e5 cd 62 10 f1 cd e5 1 af 32 a0
  //   be 21 a1 be 96 f2 72 e2 21 1 0 e5 cd 62 10 f1 79 32 a2 be cd e5 1 3a a2 be b7 28 18 3a a0 be 6f 26 0
  //   1 6c bc 9 3a 0 aa 77 21 4 0 cd 9d 27 cd 4b e4 f1 21 4 0 cd 9d 27 cd 4b e4 f1 3a a0 be 3c 32 a0 be 18
  //   b9 3a a2 be 4f c3 58 27 cd 41 27 3e 8 32 9e be cd bf b 21 1 0 e5 cd 62 10 f1 cd e5 1 af 32 9d be 21
  //   9e be 96 f2 d0 e2 21 1 0 e5 cd 62 10 f1 79 32 9f be cd e5 1 3a 9f be b7 28 e 3a 9d be 6f 26 0 1 6c
  //   bc 9 3a 0 aa 77 21 4 0 cd 9d 27 cd 4b e4 f1 3a 9d be 3c 32 9d be 18 c3 3a 9f be 4f c3 58 27 cd 41 27
  //   af 32 9b be 21 4 0 19 3a 9b be 96 f2 31 e3 21 3f d6 22 1f bc 21 6 0 19 7e 23 66 6f 7e 32 1d bc 2a 9b
  //   be 26 0 1 6c bc 9 7e 32 1e bc 3a 1c bc 3c 32 1c bc 21 6 0 cd 9d 27 21 6 0 19 34 30 2 23 34 2a 9b be
  //   26 0 1 6c bc 9 c1 a be 28 a e 0 c3 58 27 e f c3 58 27 3a 9b be 3c 32 9b be 18 9f cd 35 27 21 4 0 19
  //   7e 23 66 6f 22 1f bc 3e 0 32 1d bc 3e 1 32 1c bc 3a 36 bc e6 f 32 36 bc 3a 36 bc f6 80 32 36 bc 3a
  //   36 bc 32 0 a8 21 2 0 e5 cd 62 10 f1 79 32 7f be cd e5 1 3a 36 bc f6 1c 32 36 bc 3a 7f be b7 20 9 3a
  //   36 bc 32 0 a8 c3 3c 27 21 4 0 19 7e 23 66 6f 7e 32 1e bc 3a 1e bc b7 28 3 c3 3c 27 3e ff 32 1d bc 3e
  //   2 32 1c bc 3a 36 bc e6 f7 32 36 bc 3a 36 bc 32 0 a8 21 2 0 e5 cd 62 10 f1 79 32 7f be cd e5 1 3a 36
  //   bc f6 1c 32 36 bc 3a 7f be b7 20 9 3a 36 bc 32 0 a8 c3 3c 27 21 4 0 19 7e 23 66 6f 7e 32 1e bc 21 1d
  //   bc 3a 1e bc be 28 3 c3 3c 27 3e 3 32 1c bc 3e 0 32 1d bc 3a 36 bc e6 e7 32 36 bc 3a 36 bc 32 0 a8 21
  //   2 0 e5 cd 62 10 f1 79 32 7f be cd e5 1 3a 36 bc f6 1c 32 36 bc 3a 7f be b7 20 3 c3 3c 27 21 4 0 19
  //   7e 23 66 6f 7e 32 1e bc 3a 36 bc 32 0 a8 c3 3c 27 cd 35 27 21 4 0 19 7e b7 20 16 3a 77 bc 3c 32 77
  //   bc 32 0 c8 3a 76 bc 3c 32 76 bc 32 1 c8 18 a 3a 79 bc 3c 32 79 bc 32 3 c0 c3 3c 27 cd 35 27 3e 30 32
  //   77 bc 3e b0 32 76 bc 3e 8 32 1 c8 3e 90 32 2 c8 3e 0 32 2 c0 3e 0 32 3 c0 3e 0 32 0 c8 21 0 0 e5 cd
  //   4b e4 f1 c3 3c 27 854*ff cd f1 5e 3e 1 32 f6 b4 3e 1b 32 f7 b4 87 9f 32 f8 b4 21 f1 bc 22 f9 b4 21
  //   d6 bc 22 fb b4 21 f6 b4 e5 cd ac f2 f1 2a bf b5 7e fe 27 20 b 3a ca b6 32 23 bd cd 81 e8 18 17 21 4
  //   0 3a ca b6 4f 87 9f 47 7d 91 6f 7c 98 67 7d 32 23 bd cd a5 e9 2a c6 b4 e5 21 d6 bc c1 79 96 4f 78 23
  //   9e 47 79 32 c bd 1 1 0 c3 f8 5e 31 e9 14 0 31 e9 a 0 31 e9 5 0 b0 e8 2 0 91 e8 1 0 0 0 31 e9 cd f1
  //   5e 3a d4 bc 4f 87 9f 47 21 69 e8 c3 31 8f 2a cf bc 3a ca b6 4f 87 9f 47 7d 91 6f 7c 98 67 1 ff ff 9
  //   22 c6 b4 3e 1 32 d bd c3 f8 5e 3a ca b6 4f 87 9f 47 c5 3a d3 bc 4f 87 9f 47 e1 7d 91 6f 7c 98 67 3e
  //   1 95 3e 0 9c f2 db e8 2a cf bc 1 fe ff 9 22 c6 b4 18 1c 21 d3 bc 3a ca b6 be f2 ed e8 2a cf b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
endmodule
