// Logisim project tektronix_ttl_symbols.circ as structural Verilog: 6 circuits, main circuit ttl_74393
module ttl_74393 (
  input  CLR_A,
  input  CLK_A,
  input  CLR_B,
  input  CLK_B,
  output QA0,
  output QA1,
  output QA2,
  output QA3,
  output QB0,
  output QB1,
  output QB2,
  output QB3
);

  wire counter_1_carry, counter_2_carry, not_1_out, not_2_out;

  not not_1 (not_1_out, CLK_A);
  not not_2 (not_2_out, CLK_B);
  Counter #(.max('hf), .width(4)) counter_1 (
    .clr(CLR_A), .load(1'b0), .up(1'b1), .count(1'b1), .clk(not_1_out), .D(4'b0000), .carry(counter_1_carry),
    .Q({QA3, QA2, QA1, QA0}));
  Counter #(.max('hf), .width(4)) counter_2 (
    .clr(CLR_B), .load(1'b0), .up(1'b1), .count(1'b1), .clk(not_2_out), .D(4'b0000), .carry(counter_2_carry),
    .Q({QB3, QB2, QB1, QB0}));
  // NoConnect on counter_1_carry
  // NoConnect on counter_2_carry
endmodule

module ttl_74279_sr (
  input  S,
  input  R,
  output Q
);

  wire not_1_out, not_2_out, s_r_ff_1_qn, undriven, undriven_2;

  not not_1 (not_1_out, S);
  S_R_Flip_Flop #(.trigger("high")) s_r_ff_1 (
    .S(undriven), .R(undriven_2), .clk(1'b0), .Q(Q), .reset(not_2_out), .Qn(s_r_ff_1_qn), .preset(not_1_out));
  // NoConnect on undriven
  // NoConnect on undriven_2
  // NoConnect on s_r_ff_1_qn
  not not_2 (not_2_out, R);
endmodule

module ttl_74279_ssr (
  input  S1,
  input  S2,
  input  R,
  output Q
);

  wire not_1_out, or_1_out, s_r_ff_1_qn, undriven, undriven_2;

  not not_1 (not_1_out, R);
  or or_1 (or_1_out, ~S1, ~S2);  // OR_Gate
  S_R_Flip_Flop s_r_ff_1 (
    .S(undriven), .R(undriven_2), .clk(1'b0), .Q(Q), .reset(not_1_out), .Qn(s_r_ff_1_qn), .preset(or_1_out));
  // NoConnect on undriven
  // NoConnect on undriven_2
  // NoConnect on s_r_ff_1_qn
endmodule

module ttl_74670 (
  input  D1,
  input  GR,
  input  D2,
  input  D3,
  input  RA,
  input  D4,
  input  RB,
  input  WA,
  input  WB,
  input  GW,
  output Q1,
  output Q2,
  output Q3,
  output Q4
);

  wire decoder_1_out0, decoder_1_out1, decoder_1_out2, decoder_1_out3, not_1_out;
  wire [3:0] register_1_q, register_2_q, register_3_q, register_4_q;

  Decoder #(.enable("false"), .select(2)) decoder_1 (
    .out0(decoder_1_out0), .out1(decoder_1_out1), .out2(decoder_1_out2), .out3(decoder_1_out3), .sel({WB, WA}));
  Register #(.trigger("low"), .width(4)) register_1 (
    .D({D4, D3, D2, D1}), .en(decoder_1_out0), .clk(GW), .Q(register_1_q), .clr(1'b0));
  Register #(.trigger("low"), .width(4)) register_2 (
    .D({D4, D3, D2, D1}), .en(decoder_1_out1), .clk(GW), .Q(register_2_q), .clr(1'b0));
  Register #(.trigger("low"), .width(4)) register_3 (
    .D({D4, D3, D2, D1}), .en(decoder_1_out2), .clk(GW), .Q(register_3_q), .clr(1'b0));
  Register #(.trigger("low"), .width(4)) register_4 (
    .D({D4, D3, D2, D1}), .en(decoder_1_out3), .clk(GW), .Q(register_4_q), .clr(1'b0));
  not not_1 (not_1_out, GR);
  Multiplexer #(.disabled("Z"), .enable("true"), .select(2), .width(4)) multiplexer_1 (
    .in0(register_1_q), .in1(register_2_q), .in2(register_3_q), .in3(register_4_q), .out({Q4, Q3, Q2, Q1}),
    .sel({RB, RA}), .en(not_1_out));
endmodule

module ttl_74163 (
  input  ENT,
  input  ENP,
  input  CLR,
  input  LD,
  input  CLK,
  input  A,
  input  B,
  input  C,
  input  D,
  output RCO,
  output QA,
  output QB,
  output QC,
  output QD
);

  wire and_1_out, counter_1_carry, not_1_out, not_2_out;

  and and_1 (and_1_out, ENT, ENP);
  not not_1 (not_1_out, CLR);
  not not_2 (not_2_out, LD);
  Counter #(.max('hf), .width(4)) counter_1 (
    .clr(not_1_out), .load(not_2_out), .up(1'b1), .count(and_1_out), .clk(CLK), .D({D, C, B, A}),
    .carry(counter_1_carry), .Q({QD, QC, QB, QA}));
  and and_2 (RCO, ENT, counter_1_carry);
endmodule

module ttl_74283 (
  input  C0,
  input  A1,
  input  A2,
  input  A3,
  input  A4,
  input  B1,
  input  B2,
  input  B3,
  input  B4,
  output E1,
  output E2,
  output E3,
  output E4,
  output C4
);

  Adder #(.width(4)) adder_1 (.a({A4, A3, A2, A1}), .b({B4, B3, B2, B1}), .out({E4, E3, E2, E1}), .cin(C0), .cout(C4));
endmodule
